# Fritzing sketch night_symphony-shield (saved by Fritzing 0.9.1b)
circuit board: 6.88566cm x 5.36311cm
breadboards: 1

parts:
  J1 = male pin header, 5 pins [form="♂ (male)"]
  J2 = male pin header, 5 pins [form="♂ (male)"]
  J3 = male pin header, 5 pins [form="♂ (male)"]
  J4 = male pin header, 5 pins [form="♂ (male)"]
  J5 = male pin header, 5 pins [form="♂ (male)"]
  J6 = male pin header, 5 pins [form="♂ (male)"]
  R1 = Resistor [tolerance=±5% resistance=220 package=THT]
  R2 = Resistor [tolerance=±5% resistance=220 package=THT]
  R4 = Resistor [tolerance=±5% resistance=220 package=THT]
  R5 = Resistor [tolerance=±5% resistance=220 package=THT]
  R6 = Resistor [tolerance=±5% resistance=220 package=THT]
  R3 = Resistor [tolerance=±5% resistance=220 package=THT]
  Board = Arduino Uno (Rev3)
  LED1 = LED - 5mm [color="Red (633nm)" package="5 mm [THT]"]
  R7 = Resistor [tolerance=±5% resistance=220 package=THT]
  J8 = Power Jack [package=power_jack_pth]
  D1 = Diode [package=diode-1n4148]
  IC1 = IC, DIP package, 6 pins [chip_label=IC]
  J7 = male pin header, 4 pins [form="♂ (male)"]
  R8 = Resistor [tolerance=±5% resistance=220 package=THT]
  Q1 = npn-Powertransistor [package="TO220 [THT]"]
  Q2 = npn-Powertransistor [package="TO220 [THT]"]
  Q3 = npn-Powertransistor [package="TO220 [THT]"]
  Q4 = npn-Powertransistor [package="TO220 [THT]"]
  Q5 = npn-Powertransistor [package="TO220 [THT]"]
  Q6 = npn-Powertransistor [package="TO220 [THT]"]

nets:
  N1: J1.pin1, J3.pin1, J4.pin1, J6.pin1, J8.PWR, D1.A, J7.pin3
  N2: J1.pin2, Q1.collector
  N3: J1.pin3, J2.pin3, J3.pin3, J4.pin3, J5.pin3, J6.pin3, Board.5V, J7.pin1
  N4: J1.pin4, Board.D8
  GND: J1.pin5, J2.pin5, J3.pin5, J4.pin5, J5.pin5, J6.pin5, Board.GND, LED1.cathode, J8.GND, J7.pin2, R8.Pin_1, Q1.emitter, Q2.emitter, Q3.emitter, Q4.emitter, Q5.emitter, Q6.emitter
  N5: J2.pin1, J5.pin1
  N6: J2.pin2, Q2.collector
  N7: J2.pin4, Board.D4
  N8: J3.pin2, Q3.collector
  N9: J3.pin4, Board.A5/SCL
  N10: J4.pin2, Q4.collector
  N11: J4.pin4, Board.D12/MISO
  N12: J5.pin2, Q5.collector
  N13: J5.pin4, Board.D7
  N14: J6.pin2, Q6.collector
  N15: J6.pin4, Board.D2
  N16: R1.Pin_0, Q1.base
  N17: R1.Pin_1, Board.D10_PWM/SS
  N18: R2.Pin_0, Q2.base
  N19: R2.Pin_1, Board.D6_PWM
  N20: R4.Pin_0, Q4.base
  N21: R4.Pin_1, Board.D11_PWM/MOSI
  N22: R5.Pin_0, Q5.base
  N23: R5.Pin_1, Board.D9_PWM
  N24: R6.Pin_0, Q6.base
  N25: R6.Pin_1, Board.D5_PWM
  N26: R3.Pin_0, Q3.base
  N27: R3.Pin_1, Board.D3_PWM
  N28: Board.A0, J7.pin4
  N29: Board.A1, IC1.pin1
  N30: Board.A2, IC1.pin4
  N31: Board.A3, IC1.pin3
  N32: Board.A4/SDA, IC1.pin6
  N33: Board.D13/SCK, R7.Pin_1
  N34: Board.VIN, D1.C
  N35: LED1.anode, R7.Pin_0
  N36: IC1.pin2, IC1.pin5, R8.Pin_0

notes:
  CMoP
  Night Symphony
  v0.3

custom parts:
  npn-Powertransistor: A npn transistor which can drive a higher load
